# Fritzing sketch series (saved by Fritzing 0.9.0b)
breadboards: 1

parts:
  Part1 = Arduino Uno (Rev3)
  LED1 = LED - 5mm [color="Red (633nm)" package="5 mm [THT]"]
  R1 = Resistor [package="0402 [SMD]"]
  LED2 = LED - 5mm [color="Red (633nm)" package="5 mm [THT]"]

nets:
  N1: Part1.5V, LED1.cathode
  N2: Part1.GND, R1.Pin_1
  N3: LED1.anode, LED2.cathode
  N4: R1.Pin_0, LED2.anode
